# Fritzing sketch CircuitJeu_AntoniniTarrit (saved by Fritzing 0.9.10b)
breadboards: 2

parts:
  Componente2 = Arduino Mega 2560 (Rev3)
  S1 = Momentary Switch [package=ksa_sealed_tac_switch]
  LED1 = smd LED [color="Red (633nm)" package="1206 [SMD]"]
  LED2 = smd LED [color="Red (633nm)" package="1206 [SMD]"]
  LED3 = smd LED [color="Red (633nm)" package="1206 [SMD]"]
  LED4 = smd LED [color="Red (633nm)" package="1206 [SMD]"]
  LED5 = smd LED [color="Red (633nm)" package="1206 [SMD]"]
  LED6 = smd LED [color="Red (633nm)" package="1206 [SMD]"]
  LED7 = smd LED [color="Red (633nm)" package="1206 [SMD]"]
  LED8 = smd LED [color="Red (633nm)" package="1206 [SMD]"]
  S4 = Momentary Switch [package=ksa_sealed_tac_switch]
  S5 = Momentary Switch [package=ksa_sealed_tac_switch]
  S6 = Momentary Switch [package=ksa_sealed_tac_switch]
  S7 = Momentary Switch [package=ksa_sealed_tac_switch]
  S8 = Momentary Switch [package=ksa_sealed_tac_switch]
  S9 = Momentary Switch [package=ksa_sealed_tac_switch]
  S10 = Momentary Switch [package=ksa_sealed_tac_switch]
  R4 = Resistor [tolerance=±5% resistance=330 package="0402 [SMD]"]
  R5 = Resistor [tolerance=±5% resistance=330 package="0402 [SMD]"]
  S19 = Momentary Switch [package=ksa_sealed_tac_switch]
  S20 = Momentary Switch [package=ksa_sealed_tac_switch]
  S21 = Momentary Switch [package=ksa_sealed_tac_switch]
  S22 = Momentary Switch [package=ksa_sealed_tac_switch]
  S23 = Momentary Switch [package=ksa_sealed_tac_switch]
  S24 = Momentary Switch [package=ksa_sealed_tac_switch]
  S25 = Momentary Switch [package=ksa_sealed_tac_switch]
  S26 = Momentary Switch [package=ksa_sealed_tac_switch]
  LED17 = smd LED [color="Red (633nm)" package="1206 [SMD]"]
  LED18 = smd LED [color="Red (633nm)" package="1206 [SMD]"]
  LED19 = smd LED [color="Red (633nm)" package="1206 [SMD]"]
  LED20 = smd LED [color="Red (633nm)" package="1206 [SMD]"]
  LED21 = smd LED [color="Red (633nm)" package="1206 [SMD]"]
  LED22 = smd LED [color="Red (633nm)" package="1206 [SMD]"]
  LED23 = smd LED [color="Red (633nm)" package="1206 [SMD]"]
  LED24 = smd LED [color="Red (633nm)" package="1206 [SMD]"]

nets:
  N1: Componente2.5V, R4.Pin_0, R5.Pin_0
  N2: Componente2.GND, S1.2, S4.2, S5.2, S6.2, S7.2, S8.2, S9.2, S10.2, S19.2, S20.2, S21.2, S22.2, S23.2, S24.2, S25.2, S26.2
  N3: Componente2.D22, S1.3
  N4: Componente2.D23, S26.3
  N5: Componente2.D24, S4.3
  N6: Componente2.D25, S25.3
  N7: Componente2.D26, S7.3
  N8: Componente2.D27, S22.3
  N9: Componente2.D28, S5.3
  N10: Componente2.D29, S24.3
  N11: Componente2.D30, S6.3
  N12: Componente2.D31, S23.3
  N13: Componente2.D32, S10.3
  N14: Componente2.D33, S19.3
  N15: Componente2.D34, S8.3
  N16: Componente2.D35, S21.3
  N17: Componente2.D36, S9.3
  N18: Componente2.D37, S20.3
  N19: Componente2.D38, LED3.cathode
  N20: Componente2.D39, LED22.cathode
  N21: Componente2.D40, LED6.cathode
  N22: Componente2.D41, LED19.cathode
  N23: Componente2.D42, LED7.cathode
  N24: Componente2.D43, LED18.cathode
  N25: Componente2.D44, LED5.cathode
  N26: Componente2.D45, LED20.cathode
  N27: Componente2.D46, LED4.cathode
  N28: Componente2.D47, LED21.cathode
  N29: Componente2.D48, LED2.cathode
  N30: Componente2.D49, LED23.cathode
  N31: Componente2.D50, LED1.cathode
  N32: Componente2.D51, LED24.cathode
  N33: Componente2.D52, LED8.cathode
  N34: Componente2.D53, LED17.cathode
  N35: LED1.anode, LED2.anode, LED3.anode, LED4.anode, LED5.anode, LED6.anode, LED7.anode, LED8.anode, R4.Pin_1
  N36: R5.Pin_1, LED17.anode, LED18.anode, LED19.anode, LED20.anode, LED21.anode, LED22.anode, LED23.anode, LED24.anode
